# Fritzing sketch rpi-breadboard (saved by Fritzing 0.9.3b)
breadboards: 1

parts:
  Raspberry_Pi_1 = Raspberry Pi 3 [part_number=RPI-3-V1.2]
  J3 = T Cobbler Plus

nets:
  3V3: Raspberry_Pi_1.3v3, Raspberry_Pi_1.3V3, J3.3.3V#41, J3.3.3V#57
  N1: Raspberry_Pi_1.GPIO2, J3.GPIO_2
  N2: Raspberry_Pi_1.GPIO3, J3.GPIO_3
  N3: Raspberry_Pi_1.GIPO4, J3.GPIO_4
  N4: Raspberry_Pi_1.GND, J3.GND#46, J3.GND#49, J3.GND#54, J3.GND#60, J3.GND#65, J3.GND#70, J3.GND#74, J3.GND#79
  N5: Raspberry_Pi_1.GIPO17, J3.GPIO_17
  N6: Raspberry_Pi_1.GIPO27, J3.GPIO_27
  N7: Raspberry_Pi_1.GIPO22, J3.GPIO_22
  N8: Raspberry_Pi_1.GIPO10, J3.GPIO_10
  N9: Raspberry_Pi_1.GIPO9, J3.GPIO_9
  N10: Raspberry_Pi_1.GIPO11, J3.GPIO_11
  N11: Raspberry_Pi_1.ID_SD, J3.ID_SD
  N12: Raspberry_Pi_1.GIPO5, J3.GPIO_5
  N13: Raspberry_Pi_1.GIPO6, J3.GPIO_6
  N14: Raspberry_Pi_1.GIPO13, J3.GPIO_13
  N15: Raspberry_Pi_1.GIPO19, J3.GPIO_19
  N16: Raspberry_Pi_1.GIPO26, J3.GPIO_26
  N17: Raspberry_Pi_1.GIPO21, J3.GPIO_21
  N18: Raspberry_Pi_1.GIPO20, J3.GPIO_20
  N19: Raspberry_Pi_1.GIPO16, J3.GPIO_16
  N20: Raspberry_Pi_1.GIPO12, J3.GPIO_12
  N21: Raspberry_Pi_1.ID_SC, J3.ID_SC
  N22: Raspberry_Pi_1.GIPO7, J3.GPIO_7
  N23: Raspberry_Pi_1.GIPO8, J3.GPIO_8
  N24: Raspberry_Pi_1.GIPO25, J3.GPIO_25
  N25: Raspberry_Pi_1.GIPO24, J3.GPIO_24
  N26: Raspberry_Pi_1.GIPO23, J3.GPIO_23
  N27: Raspberry_Pi_1.GIPO18, J3.GPIO_18
  N28: Raspberry_Pi_1.GIPO15, J3.GPIO_15
  N29: Raspberry_Pi_1.GIPO14, J3.GPIO_14
  5V: Raspberry_Pi_1.5V, J3.5V

custom parts:
  T Cobbler Plus: The T-Cobbler Plus is an add on prototyping board from Adafruit specifically designed for the Raspberry Pi B+ that can break out all those tasty power, GPIO, I2C and SPI pins from the 40-pin header onto a solderless breadboard. This set will make "cobbling together" prototypes with the Pi super easy. The T-Cobbler Plus can plug into any solderless breadboard.
