# Fritzing sketch rpi-breadboard2 (saved by Fritzing 0.9.2b)
breadboards: 1

parts:
  Raspberry_Pi_1 = Raspberry Pi 3 [part_number=RPI-3-V1.2]  # not connected
  J1 = T Cobbler Plus
  S1 = H-Bridge with L298N
  M1 = DC Motor
  VCC1 = Battery
  VCC2 = Battery
  M2 = DC Motor

nets:
  N1: J1.5.0V#1, S1.5V
  N2: J1.GND#5, S1.GND, VCC1.-
  N3: J1.#27, S1.ENA
  N4: J1.#22, S1.IN1
  N5: S1.12V, VCC2.+
  N6: S1.M1-01, M2.pin_2
  N7: S1.M1-02, M2.pin_1
  N8: S1.M2-01, M1.pin_1
  N9: S1.M2-02, M1.pin_2
  N10: VCC1.+, VCC2.-

custom parts:
  T Cobbler Plus: The T-Cobbler Plus is an add on prototyping board from Adafruit specifically designed for the Raspberry Pi B+ that can break out all those tasty power, GPIO, I2C and SPI pins from the 40-pin header onto a solderless breadboard. This set will make "cobbling together" prototypes with the Pi super easy. The T-Cobbler Plus can plug into any solderless breadboard.
  H-Bridge with L298N: h-bridge
