# Fritzing sketch rpi-breadboard22 (saved by Fritzing 0.9.3b)
breadboards: 1

parts:
  Raspberry_Pi_1 = Raspberry Pi 3 [part_number=RPI-3-V1.2]  # not connected
  J1 = T Cobbler Plus
  M1 = DC Motor
  M2 = DC Motor
  VCC1 = 4 x AAA Battery Mount
  S1 = H-Bridge with L298N
  Componente1 = SRF05 Ultrasonic Rangefinder
  R1 = Resistor [tolerance=±5% resistance=1k package="0603 [SMD]"]
  R2 = Resistor [tolerance=±5% resistance=2.2k package="0805 [SMD]"]

nets:
  N1: J1.5.0V#1, Componente1.VCC
  GND: J1.GND#5, VCC1.-, S1.GND, Componente1.GND, R2.Pin_1
  N2: J1.#27, S1.IN1
  N3: J1.#22, S1.IN2
  N4: J1.#23, Componente1.Trig
  N5: J1.#24, R1.Pin_1, R2.Pin_0
  N6: J1.#5, S1.IN3
  N7: J1.#6, S1.IN4
  N8: M1.pin_1, S1.M2-01
  N9: M1.pin_2, S1.M2-02
  N10: M2.pin_1, S1.M1-02
  N11: M2.pin_2, S1.M1-01
  N12: VCC1.+, S1.12V
  N13: S1.ENA, S1.ENA-5V
  N14: S1.ENB, S1.ENB-5V
  N15: Componente1.Echo, R1.Pin_0

custom parts:
  T Cobbler Plus: The T-Cobbler Plus is an add on prototyping board from Adafruit specifically designed for the Raspberry Pi B+ that can break out all those tasty power, GPIO, I2C and SPI pins from the 40-pin header onto a solderless breadboard. This set will make "cobbling together" prototypes with the Pi super easy. The T-Cobbler Plus can plug into any solderless breadboard.
  H-Bridge with L298N: h-bridge
